// Logisim project base.circ as structural Verilog
module base_00 (
  input  D,
  input  C,
  input  B,
  input  A,
  output a_2,
  output b_2,
  output c_2,
  output d_2,
  output e,
  output f,
  output g
);

  wire nand_1_out, nand_5_out, nand_6_out, nand_7_out, nand_10_out, nand_11_out;

  nand nand_1 (nand_1_out, D, D);
  nand nand_2 (b_2, D, D);
  nand nand_3 (c_2, B, B);
  nand nand_4 (d_2, A, A);
  nand nand_5 (nand_5_out, D, D);
  nand nand_6 (nand_6_out, B, B);
  nand nand_7 (nand_7_out, A, A);
  nand nand_8 (a_2, A, nand_1_out);
  nand nand_9 (e, A, nand_5_out);
  nand nand_10 (nand_10_out, nand_6_out, nand_7_out);
  nand nand_11 (nand_11_out, D, D);
  nand nand_12 (f, nand_10_out, nand_11_out);

  assign g = B;
endmodule
